# Fritzing sketch arduino_nn (saved by Fritzing 0.9.3b)
breadboards: 1

parts:
  Arduino_Nano = Arduino Nano (Rev3.0)
  P0 = Rotary Potentiometer (Small) [maximum_resistance=100kΩ package=THT]
  P1 = Rotary Potentiometer (Small) [maximum_resistance=100kΩ package=THT]
  P2 = Rotary Potentiometer (Small) [maximum_resistance=100kΩ package=THT]
  P3 = Rotary Potentiometer (Small) [maximum_resistance=100kΩ package=THT]
  P4 = Rotary Potentiometer (Small) [maximum_resistance=100kΩ package=THT]
  P5 = Rotary Potentiometer (Small) [maximum_resistance=100kΩ package=THT]
  R1 = Resistor [tolerance=±5% resistance=330 package=THT]
  LED1 = LED - 3mm [color="Red (633nm)" package="3 mm [THT]"]
  S1 = SWITCH-MOMENTARY-2 [package=tactile_switch_smd-2]
  R2 = Resistor [tolerance=±5% resistance=330 package=THT]
  LED2 = LED - 3mm [color="Red (633nm)" package="3 mm [THT]"]
  S2 = SWITCH-MOMENTARY-2 [package=tactile_switch_smd-2]
  U1 = SWITCH_SPDT [package=kps-1290]
  R3 = Resistor [tolerance=±5% resistance=330 package=THT]
  LED3 = LED - 3mm [color="Red (633nm)" package="3 mm [THT]"]

nets:
  GND: Arduino_Nano.GND, P0.leg1, P1.leg1, P2.leg1, P3.leg1, P4.leg1, P5.leg1, S1.2, S2.2, U1.S, LED3.cathode
  N1: Arduino_Nano.D2, R1.Pin_0, S1.1
  N2: Arduino_Nano.D4, R2.Pin_0, S2.1
  N3: Arduino_Nano.D7, U1.P
  N4: Arduino_Nano.D12/MISO, R3.Pin_0
  5V: Arduino_Nano.5V, P0.leg2, P1.leg2, P2.leg2, P3.leg2, P4.leg2, P5.leg2, LED1.anode, LED2.anode
  N5: Arduino_Nano.A5, P5.wiper
  N6: Arduino_Nano.A4, P4.wiper
  N7: Arduino_Nano.A3, P3.wiper
  N8: Arduino_Nano.A2, P2.wiper
  N9: Arduino_Nano.A1, P1.wiper
  N10: Arduino_Nano.A0, P0.wiper
  N11: R1.Pin_1, LED1.cathode
  N12: R2.Pin_1, LED2.cathode
  N13: R3.Pin_1, LED3.anode
